// Logisim project KiKi_Pi_One.circ as structural Verilog
module Register_A (
  input  [15:0] Data_in,
  input  Load,
  input  CLK,
  output [15:0] Data_out
);

  Register #(.width(16)) register_1 (.D(Data_in), .en(Load), .clk(CLK), .Q(Data_out));  // open: clr
endmodule

module Register_D (
  input  [15:0] Data_in,
  input  Load,
  input  CLK,
  output [15:0] Data_out
);

  Register #(.width(16)) register_1 (.D(Data_in), .en(Load), .clk(CLK), .Q(Data_out));  // open: clr
endmodule
